// Logisim project deco4_16.circ as structural Verilog: 1 circuit, main circuit decodeur4_16
module decodeur4_16 (
  input  [3:0] entree,
  output out_2,
  output out_3,
  output out_4,
  output out_5,
  output out_6,
  output out_7,
  output out_8,
  output out_9,
  output out_10,
  output out_11,
  output out_12,
  output out_13,
  output out_14,
  output out_15,
  output out_16,
  output out_17
);

  wire and_1_out, and_2_out, and_3_out, and_4_out, and_5_out, and_6_out, and_7_out, and_8_out, and_9_out,
       and_10_out, and_11_out, and_12_out, and_13_out, and_14_out, and_15_out, and_16_out, and_17_out,
       and_18_out, and_19_out, and_20_out, and_21_out, and_22_out, and_23_out, and_24_out, and_25_out,
       and_26_out, and_27_out, and_28_out, and_29_out, and_30_out, and_31_out, and_32_out, not_1_out,
       not_2_out, not_3_out, not_4_out, not_5_out, not_6_out, not_7_out, not_8_out, not_9_out, not_10_out,
       not_11_out, not_12_out, not_13_out, not_14_out, not_15_out, not_16_out, not_17_out, not_18_out,
       not_19_out, not_20_out, not_21_out, not_22_out, not_23_out, not_24_out, not_25_out, not_26_out,
       not_27_out, not_28_out, not_29_out, not_30_out, not_31_out, not_32_out;

  not not_1 (not_1_out, entree[3]);
  and and_1 (and_1_out, not_1_out, not_2_out);
  not not_2 (not_2_out, entree[2]);
  not not_3 (not_3_out, entree[1]);
  and and_2 (and_2_out, not_3_out, not_4_out);
  not not_4 (not_4_out, entree[0]);
  not not_5 (not_5_out, entree[3]);
  and and_3 (and_3_out, not_5_out, not_6_out);
  not not_6 (not_6_out, entree[2]);
  not not_7 (not_7_out, entree[1]);
  and and_4 (and_4_out, not_7_out, entree[0]);
  not not_8 (not_8_out, entree[3]);
  and and_5 (and_5_out, not_8_out, not_9_out);
  not not_9 (not_9_out, entree[2]);
  and and_6 (and_6_out, entree[1], not_10_out);
  not not_10 (not_10_out, entree[0]);
  not not_11 (not_11_out, entree[3]);
  and and_7 (and_7_out, not_11_out, not_12_out);
  not not_12 (not_12_out, entree[2]);
  and and_8 (and_8_out, entree[1], entree[0]);
  not not_13 (not_13_out, entree[3]);
  and and_9 (and_9_out, not_13_out, entree[2]);
  not not_14 (not_14_out, entree[1]);
  and and_10 (and_10_out, not_14_out, not_15_out);
  not not_15 (not_15_out, entree[0]);
  not not_16 (not_16_out, entree[3]);
  and and_11 (and_11_out, not_16_out, entree[2]);
  not not_17 (not_17_out, entree[1]);
  and and_12 (and_12_out, not_17_out, entree[0]);
  not not_18 (not_18_out, entree[3]);
  and and_13 (and_13_out, not_18_out, entree[2]);
  and and_14 (and_14_out, entree[1], not_19_out);
  not not_19 (not_19_out, entree[0]);
  not not_20 (not_20_out, entree[3]);
  and and_15 (and_15_out, not_20_out, entree[2]);
  and and_16 (and_16_out, entree[1], entree[0]);
  and and_17 (and_17_out, entree[3], not_21_out);
  not not_21 (not_21_out, entree[2]);
  not not_22 (not_22_out, entree[1]);
  and and_18 (and_18_out, not_22_out, not_23_out);
  not not_23 (not_23_out, entree[0]);
  and and_19 (and_19_out, entree[3], not_24_out);
  not not_24 (not_24_out, entree[2]);
  not not_25 (not_25_out, entree[1]);
  and and_20 (and_20_out, not_25_out, entree[0]);
  and and_21 (and_21_out, entree[3], not_26_out);
  not not_26 (not_26_out, entree[2]);
  and and_22 (and_22_out, entree[1], not_27_out);
  not not_27 (not_27_out, entree[0]);
  and and_23 (and_23_out, entree[3], not_28_out);
  not not_28 (not_28_out, entree[2]);
  and and_24 (and_24_out, entree[1], entree[0]);
  and and_25 (and_25_out, entree[3], entree[2]);
  not not_29 (not_29_out, entree[1]);
  and and_26 (and_26_out, not_29_out, not_30_out);
  not not_30 (not_30_out, entree[0]);
  and and_27 (and_27_out, entree[3], entree[2]);
  not not_31 (not_31_out, entree[1]);
  and and_28 (and_28_out, not_31_out, entree[0]);
  and and_29 (and_29_out, entree[3], entree[2]);
  and and_30 (and_30_out, entree[1], not_32_out);
  not not_32 (not_32_out, entree[0]);
  and and_31 (and_31_out, entree[3], entree[2]);
  and and_32 (and_32_out, entree[1], entree[0]);
  and and_33 (out_2, and_1_out, and_2_out);
  and and_34 (out_3, and_3_out, and_4_out);
  and and_35 (out_4, and_5_out, and_6_out);
  and and_36 (out_5, and_7_out, and_8_out);
  and and_37 (out_6, and_9_out, and_10_out);
  and and_38 (out_7, and_11_out, and_12_out);
  and and_39 (out_8, and_13_out, and_14_out);
  and and_40 (out_9, and_15_out, and_16_out);
  and and_41 (out_10, and_17_out, and_18_out);
  and and_42 (out_11, and_19_out, and_20_out);
  and and_43 (out_12, and_21_out, and_22_out);
  and and_44 (out_13, and_23_out, and_24_out);
  and and_45 (out_14, and_25_out, and_26_out);
  and and_46 (out_15, and_27_out, and_28_out);
  and and_47 (out_16, and_29_out, and_30_out);
  and and_48 (out_17, and_31_out, and_32_out);
endmodule
